// Logisim project MERT_2453025_ALU8.circ as structural Verilog
module FADDER8 (
  input  [7:0] X,
  input  CIN,
  input  [7:0] Y,
  output [7:0] SUM,
  output COUT
);

  wire fadder1_1_cout, fadder1_2_cout, fadder1_3_cout, fadder1_4_cout, fadder1_5_cout, fadder1_6_cout,
       fadder1_7_cout;

  FADDER1 fadder1_1 (.A(X[0]), .B(Y[0]), .CIN(CIN), .SUM(SUM[0]), .COUT(fadder1_1_cout));
  FADDER1 fadder1_2 (.A(X[1]), .B(Y[1]), .CIN(fadder1_1_cout), .SUM(SUM[1]), .COUT(fadder1_2_cout));
  FADDER1 fadder1_3 (.A(X[2]), .B(Y[2]), .CIN(fadder1_2_cout), .SUM(SUM[2]), .COUT(fadder1_3_cout));
  FADDER1 fadder1_4 (.A(X[3]), .B(Y[3]), .CIN(fadder1_3_cout), .SUM(SUM[3]), .COUT(fadder1_4_cout));
  FADDER1 fadder1_5 (.A(X[4]), .B(Y[4]), .CIN(fadder1_4_cout), .SUM(SUM[4]), .COUT(fadder1_5_cout));
  FADDER1 fadder1_6 (.A(X[5]), .B(Y[5]), .CIN(fadder1_5_cout), .SUM(SUM[5]), .COUT(fadder1_6_cout));
  FADDER1 fadder1_7 (.A(X[6]), .B(Y[6]), .CIN(fadder1_6_cout), .SUM(SUM[6]), .COUT(fadder1_7_cout));
  FADDER1 fadder1_8 (.A(X[7]), .B(Y[7]), .CIN(fadder1_7_cout), .SUM(SUM[7]), .COUT(COUT));

  // Notes on the sheet:
  //   D0
  //   D1
  //   D2
  //   D3
  //   D4
  //   D5
  //   D6
  //   D7
endmodule

module FADDER1 (
  input  A,
  input  B,
  input  CIN,
  output SUM,
  output COUT
);

  wire and_1_out, and_2_out, xor_1_out;

  xor xor_1 (xor_1_out, A, B);
  and and_1 (and_1_out, xor_1_out, CIN);
  and and_2 (and_2_out, A, B);
  xor xor_2 (SUM, xor_1_out, CIN);
  or or_1 (COUT, and_1_out, and_2_out);
endmodule

module ALU8 (
  input  [7:0] X,
  input  [7:0] Y,
  input  [1:0] opcode,
  output [7:0] RESULT,
  output EQ,
  output OVF,
  output CF,
  output ZF,
  output SF
);

  wire [7:0] and_1_out, fadder8_1_sum, or_1_out, rotl_1_r, xnor_1_out;

  assign and_1_out = X & Y;  // AND_Gate and_1, 8 bits wide
  assign or_1_out = X | Y;  // OR_Gate or_1, 8 bits wide
  assign xnor_1_out = ~(X ^ Y);  // XNOR_Gate xnor_1, 8 bits wide
  FADDER8 fadder8_1 (.X(X), .CIN(opcode[0]), .Y(Y), .SUM(fadder8_1_sum), .COUT(CF));
  rotl rotl_1 (.A(X), .B(Y[2:0]), .R(rotl_1_r));
  and and_2 (EQ, xnor_1_out[0], xnor_1_out[1], xnor_1_out[2], xnor_1_out[3], xnor_1_out[4], xnor_1_out[5], xnor_1_out[6], xnor_1_out[7]);
  xor xor_1 (OVF, CF, opcode[0]);
  Multiplexer #(.select(2), .width(8)) multiplexer_1 (
    .in0(fadder8_1_sum), .in1(and_1_out), .in2(or_1_out), .in3(rotl_1_r), .out(RESULT), .sel(opcode));
  nor nor_1 (ZF, RESULT[0], RESULT[1], RESULT[2], RESULT[3], RESULT[4], RESULT[5], RESULT[6], RESULT[7]);

  assign SF = RESULT[7];
endmodule

module rotl (
  input  [7:0] A,
  input  [2:0] B,
  output [7:0] R
);

  Multiplexer #(.select(3)) multiplexer_1 (
    .in0(A[7]), .in1(A[6]), .in2(A[5]), .in3(A[4]), .in4(A[3]), .in5(A[2]), .in6(A[1]), .in7(A[0]),
    .out(R[7]), .sel(B));
  Multiplexer #(.select(3)) multiplexer_2 (
    .in0(A[6]), .in1(A[5]), .in2(A[4]), .in3(A[3]), .in4(A[2]), .in5(A[1]), .in6(A[0]), .in7(A[7]),
    .out(R[6]), .sel(B));
  Multiplexer #(.select(3)) multiplexer_3 (
    .in0(A[5]), .in1(A[4]), .in2(A[3]), .in3(A[2]), .in4(A[1]), .in5(A[0]), .in6(A[7]), .in7(A[6]),
    .out(R[5]), .sel(B));
  Multiplexer #(.select(3)) multiplexer_4 (
    .in0(A[4]), .in1(A[3]), .in2(A[2]), .in3(A[1]), .in4(A[0]), .in5(A[7]), .in6(A[6]), .in7(A[5]),
    .out(R[4]), .sel(B));
  Multiplexer #(.select(3)) multiplexer_5 (
    .in0(A[3]), .in1(A[2]), .in2(A[1]), .in3(A[0]), .in4(A[7]), .in5(A[6]), .in6(A[5]), .in7(A[4]),
    .out(R[3]), .sel(B));
  Multiplexer #(.select(3)) multiplexer_6 (
    .in0(A[2]), .in1(A[1]), .in2(A[0]), .in3(A[7]), .in4(A[6]), .in5(A[5]), .in6(A[4]), .in7(A[3]),
    .out(R[2]), .sel(B));
  Multiplexer #(.select(3)) multiplexer_7 (
    .in0(A[1]), .in1(A[0]), .in2(A[7]), .in3(A[6]), .in4(A[5]), .in5(A[4]), .in6(A[3]), .in7(A[2]),
    .out(R[1]), .sel(B));
  Multiplexer #(.select(3)) multiplexer_8 (
    .in0(A[0]), .in1(A[7]), .in2(A[6]), .in3(A[5]), .in4(A[4]), .in5(A[3]), .in6(A[2]), .in7(A[1]),
    .out(R[0]), .sel(B));

  // Notes on the sheet:
  //   D7
  //   D6
  //   D5
  //   D4
  //   D3
  //   D2
  //   D1
  //   D0
  //   rotl
endmodule
