// Logisim project MERT_2453025_FADDER8.circ as structural Verilog: 2 circuits, main circuit FADDER8
module FADDER8 (
  input  [7:0] X,
  input  CIN,
  input  [7:0] Y,
  output [7:0] SUM,
  output COUT
);

  wire D0_cout, D1_cout, D2_cout, D3_cout, D4_cout, D5_cout, D6_cout;

  fadder_1bitt D0 (.A(X[0]), .B(Y[0]), .CIN(CIN), .S(SUM[0]), .COUT(D0_cout));
  fadder_1bitt D1 (.A(X[1]), .B(Y[1]), .CIN(D0_cout), .S(SUM[1]), .COUT(D1_cout));
  fadder_1bitt D2 (.A(X[2]), .B(Y[2]), .CIN(D1_cout), .S(SUM[2]), .COUT(D2_cout));
  fadder_1bitt D3 (.A(X[3]), .B(Y[3]), .CIN(D2_cout), .S(SUM[3]), .COUT(D3_cout));
  fadder_1bitt D4 (.A(X[4]), .B(Y[4]), .CIN(D3_cout), .S(SUM[4]), .COUT(D4_cout));
  fadder_1bitt D5 (.A(X[5]), .B(Y[5]), .CIN(D4_cout), .S(SUM[5]), .COUT(D5_cout));
  fadder_1bitt D6 (.A(X[6]), .B(Y[6]), .CIN(D5_cout), .S(SUM[6]), .COUT(D6_cout));
  fadder_1bitt D7 (.A(X[7]), .B(Y[7]), .CIN(D6_cout), .S(SUM[7]), .COUT(COUT));
endmodule

module fadder_1bitt (
  input  A,
  input  B,
  input  CIN,
  output S,
  output COUT
);

  wire and_1_out, and_2_out, xor_1_out;

  xor xor_1 (xor_1_out, A, B);
  and and_1 (and_1_out, xor_1_out, CIN);
  and and_2 (and_2_out, A, B);
  xor xor_2 (S, xor_1_out, CIN);
  or or_1 (COUT, and_1_out, and_2_out);
endmodule
