// Logisim project MERT_2453025_rotl.circ as structural Verilog: 1 circuit, main circuit rotl
module rotl (
  input  [7:0] A,
  input  [2:0] B,
  output [7:0] out_3
);

  Multiplexer #(.select(3)) multiplexer_1 (
    .in0(A[7]), .in1(A[6]), .in2(A[5]), .in3(A[4]), .in4(A[3]), .in5(A[2]), .in6(A[1]), .in7(A[0]),
    .out(out_3[7]), .sel(B));
  Multiplexer #(.select(3)) multiplexer_2 (
    .in0(A[6]), .in1(A[5]), .in2(A[4]), .in3(A[3]), .in4(A[2]), .in5(A[1]), .in6(A[0]), .in7(A[7]),
    .out(out_3[6]), .sel(B));
  Multiplexer #(.select(3)) multiplexer_3 (
    .in0(A[5]), .in1(A[4]), .in2(A[3]), .in3(A[2]), .in4(A[1]), .in5(A[0]), .in6(A[7]), .in7(A[6]),
    .out(out_3[5]), .sel(B));
  Multiplexer #(.select(3)) multiplexer_4 (
    .in0(A[4]), .in1(A[3]), .in2(A[2]), .in3(A[1]), .in4(A[0]), .in5(A[7]), .in6(A[6]), .in7(A[5]),
    .out(out_3[4]), .sel(B));
  Multiplexer #(.select(3)) multiplexer_5 (
    .in0(A[3]), .in1(A[2]), .in2(A[1]), .in3(A[0]), .in4(A[7]), .in5(A[6]), .in6(A[5]), .in7(A[4]),
    .out(out_3[3]), .sel(B));
  Multiplexer #(.select(3)) multiplexer_6 (
    .in0(A[2]), .in1(A[1]), .in2(A[0]), .in3(A[7]), .in4(A[6]), .in5(A[5]), .in6(A[4]), .in7(A[3]),
    .out(out_3[2]), .sel(B));
  Multiplexer #(.select(3)) multiplexer_7 (
    .in0(A[1]), .in1(A[0]), .in2(A[7]), .in3(A[6]), .in4(A[5]), .in5(A[4]), .in6(A[3]), .in7(A[2]),
    .out(out_3[1]), .sel(B));
  Multiplexer #(.select(3)) multiplexer_8 (
    .in0(A[0]), .in1(A[7]), .in2(A[6]), .in3(A[5]), .in4(A[4]), .in5(A[3]), .in6(A[2]), .in7(A[1]),
    .out(out_3[0]), .sel(B));

  // Notes on the sheet:
  //   D7
  //   D6
  //   D5
  //   D4
  //   D3
  //   D2
  //   D1
  //   D0
  //   rotl
endmodule
