// Logisim project MERT_2453025_rotr.circ as structural Verilog: 1 circuit, main circuit rotr
module rotr (
  input  [7:0] in_1,
  input  [2:0] B,
  output [7:0] rotr
);

  Multiplexer #(.select(3)) multiplexer_1 (
    .in0(in_1[7]), .in1(in_1[0]), .in2(in_1[1]), .in3(in_1[2]), .in4(in_1[3]), .in5(in_1[4]), .in6(in_1[5]),
    .in7(in_1[6]), .out(rotr[7]), .sel(B));
  Multiplexer #(.select(3)) multiplexer_2 (
    .in0(in_1[6]), .in1(in_1[7]), .in2(in_1[0]), .in3(in_1[1]), .in4(in_1[2]), .in5(in_1[3]), .in6(in_1[4]),
    .in7(in_1[5]), .out(rotr[6]), .sel(B));
  Multiplexer #(.select(3)) multiplexer_3 (
    .in0(in_1[5]), .in1(in_1[6]), .in2(in_1[7]), .in3(in_1[0]), .in4(in_1[1]), .in5(in_1[2]), .in6(in_1[3]),
    .in7(in_1[4]), .out(rotr[5]), .sel(B));
  Multiplexer #(.select(3)) multiplexer_4 (
    .in0(in_1[4]), .in1(in_1[5]), .in2(in_1[6]), .in3(in_1[7]), .in4(in_1[0]), .in5(in_1[1]), .in6(in_1[2]),
    .in7(in_1[3]), .out(rotr[4]), .sel(B));
  Multiplexer #(.select(3)) multiplexer_5 (
    .in0(in_1[3]), .in1(in_1[4]), .in2(in_1[5]), .in3(in_1[6]), .in4(in_1[7]), .in5(in_1[0]), .in6(in_1[1]),
    .in7(in_1[2]), .out(rotr[3]), .sel(B));
  Multiplexer #(.select(3)) multiplexer_6 (
    .in0(in_1[2]), .in1(in_1[3]), .in2(in_1[4]), .in3(in_1[5]), .in4(in_1[6]), .in5(in_1[7]), .in6(in_1[0]),
    .in7(in_1[1]), .out(rotr[2]), .sel(B));
  Multiplexer #(.select(3)) multiplexer_7 (
    .in0(in_1[1]), .in1(in_1[2]), .in2(in_1[3]), .in3(in_1[4]), .in4(in_1[5]), .in5(in_1[6]), .in6(in_1[7]),
    .in7(in_1[0]), .out(rotr[1]), .sel(B));
  Multiplexer #(.select(3)) multiplexer_8 (
    .in0(in_1[0]), .in1(in_1[1]), .in2(in_1[2]), .in3(in_1[3]), .in4(in_1[4]), .in5(in_1[5]), .in6(in_1[6]),
    .in7(in_1[7]), .out(rotr[0]), .sel(B));

  // Notes on the sheet:
  //   A
  //   D7
  //   D6
  //   D5
  //   D4
  //   D3
  //   D2
  //   D1
  //   D0
endmodule
