// Logisim project mert_2453025.circ as structural Verilog: 6 circuits, main circuit main
module main (
  input  in_1,
  input  in_2,
  input  in_3
);

  wire clock_1_out, controlunit_1_mr, controlunit_1_mux2, controlunit_1_mw, controlunit_1_we;
  wire [1:0] controlunit_1_alufunc, controlunit_1_mux1;
  wire [7:0] alu_8_1_result, multiplexer_1_out, multiplexer_2_out, ramm_1_outp, regfile_1_data1,
       regfile_1_data2, romm_1_data;
  wire [9:0] adder_1_out, register_1_q;
  wire [20:8] romm_1_data_2;

  Clock clock_1 (.out(clock_1_out));
  Register #(.trigger("falling"), .width(10)) register_1 (
    .D(adder_1_out), .en(in_2), .clk(clock_1_out), .Q(register_1_q), .clr(in_3));
  Adder #(.width(10)) adder_1 (.a(10'h1), .b(register_1_q), .out(adder_1_out), .cin(in_1));  // open: cout
  ROMM romm_1 (.address(register_1_q), .data({romm_1_data_2, romm_1_data}));
  Multiplexer #(.select(2), .width(8)) multiplexer_1 (
    .in0(alu_8_1_result), .in1(ramm_1_outp), .in2(romm_1_data), .out(multiplexer_1_out),
    .sel(controlunit_1_mux1));  // open: in3
  ControlUnit controlunit_1 (
    .Opcode(romm_1_data_2[20:17]), .mux1(controlunit_1_mux1), .MR(controlunit_1_mr),
    .mux2(controlunit_1_mux2), .WE(controlunit_1_we), .MW(controlunit_1_mw), .ALUfunc(controlunit_1_alufunc));
  RegFile regfile_1 (
    .WE(controlunit_1_we), .writeRegister(romm_1_data_2[10:8]), .writeData(multiplexer_1_out),
    .read1(romm_1_data_2[16:14]), .read2(romm_1_data_2[13:11]), .data1(regfile_1_data1),
    .data2(regfile_1_data2));
  Multiplexer #(.width(8)) multiplexer_2 (
    .in0(regfile_1_data2), .in1(romm_1_data), .out(multiplexer_2_out), .sel(controlunit_1_mux2));
  ALU_8 alu_8_1 (.X(regfile_1_data1), .Y(multiplexer_2_out), .ALUfunc(controlunit_1_alufunc), .RESULT(alu_8_1_result));
  RAMM ramm_1 (
    .address(alu_8_1_result), .WE(controlunit_1_mw), .OutE(controlunit_1_mr), .inp(regfile_1_data2),
    .outp(ramm_1_outp));
endmodule

module ALU_8 (
  input  [7:0] X,
  input  [7:0] Y,
  input  [1:0] ALUfunc,
  output [7:0] RESULT
);

  wire [7:0] adder_1_out, and_1_out, or_1_out, shifter_1_out;

  Adder adder_1 (.a(X), .b(Y), .out(adder_1_out));  // open: cin, cout
  Shifter #(.shift("rl")) shifter_1 (.in(X), .\dist (Y[2:0]), .out(shifter_1_out));
  assign and_1_out = X & Y;  // AND_Gate and_1, 8 bits wide
  assign or_1_out = X | Y;  // OR_Gate or_1, 8 bits wide
  Multiplexer #(.select(2), .width(8)) multiplexer_1 (
    .in0(adder_1_out), .in1(and_1_out), .in2(or_1_out), .in3(shifter_1_out), .out(RESULT), .sel(ALUfunc));
endmodule

module RAMM (
  input  [7:0] address,
  input  WE,
  input  OutE,
  input  [7:0] inp,
  output [7:0] outp
);

  wire Clk_out;

  Clock Clk (.out(Clk_out));
  RAM #(.asyncread("true"), .trigger("falling")) ram_1 (
    .addr(address), .we(WE), .oe(OutE), .clk(Clk_out), .din(inp), .dout(outp));
endmodule

module ROMM (
  input  [9:0] address,
  output [20:0] data
);

  ROM #(.addrWidth(10), .dataWidth(21), .misaligned("true")) ProgramROM (.addr(address), .data(data));

  // Notes on the sheet:
  //   contents of ProgramROM (hex, n*v repeats v):
  //   60108 60204 88b00 8c00 188d00 45000 24600
endmodule

module RegFile (
  input  WE,
  input  [2:0] writeRegister,
  input  [7:0] writeData,
  input  [2:0] read1,
  input  [2:0] read2,
  output [7:0] data1,
  output [7:0] data2
);

  wire clock_1_out, decoder_1_out0, decoder_1_out1, decoder_1_out2, decoder_1_out3, decoder_1_out4,
       decoder_1_out5, decoder_1_out6, decoder_1_out7;
  wire [7:0] register_1_q, register_2_q, register_3_q, register_4_q, register_5_q, register_6_q,
       register_7_q, register_8_q;

  Decoder #(.select(3)) decoder_1 (
    .out0(decoder_1_out0), .out1(decoder_1_out1), .out2(decoder_1_out2), .out3(decoder_1_out3),
    .out4(decoder_1_out4), .out5(decoder_1_out5), .out6(decoder_1_out6), .out7(decoder_1_out7),
    .sel(writeRegister), .en(WE));
  Clock clock_1 (.out(clock_1_out));
  Multiplexer #(.select(3), .width(8)) multiplexer_1 (
    .in0(register_1_q), .in1(register_2_q), .in2(register_3_q), .in3(register_4_q), .in4(register_5_q),
    .in5(register_6_q), .in6(register_7_q), .in7(register_8_q), .out(data1), .sel(read1));
  Multiplexer #(.select(3), .width(8)) multiplexer_2 (
    .in0(register_1_q), .in1(register_2_q), .in2(register_3_q), .in3(register_4_q), .in4(register_5_q),
    .in5(register_6_q), .in6(register_7_q), .in7(register_8_q), .out(data2), .sel(read2));
  Register #(.trigger("falling")) register_1 (
    .D(writeData), .en(decoder_1_out0), .clk(clock_1_out), .Q(register_1_q));  // open: clr
  Register #(.trigger("falling")) register_2 (
    .D(writeData), .en(decoder_1_out1), .clk(clock_1_out), .Q(register_2_q));  // open: clr
  Register #(.trigger("falling")) register_3 (
    .D(writeData), .en(decoder_1_out2), .clk(clock_1_out), .Q(register_3_q));  // open: clr
  Register #(.trigger("falling")) register_4 (
    .D(writeData), .en(decoder_1_out3), .clk(clock_1_out), .Q(register_4_q));  // open: clr
  Register #(.trigger("falling")) register_5 (
    .D(writeData), .en(decoder_1_out4), .clk(clock_1_out), .Q(register_5_q));  // open: clr
  Register #(.trigger("falling")) register_6 (
    .D(writeData), .en(decoder_1_out5), .clk(clock_1_out), .Q(register_6_q));  // open: clr
  Register #(.trigger("falling")) register_7 (
    .D(writeData), .en(decoder_1_out6), .clk(clock_1_out), .Q(register_7_q));  // open: clr
  Register #(.trigger("falling")) register_8 (
    .D(writeData), .en(decoder_1_out7), .clk(clock_1_out), .Q(register_8_q));  // open: clr
endmodule

module ControlUnit (
  input  [3:0] Opcode,
  output [1:0] mux1,
  output MR,
  output mux2,
  output WE,
  output MW,
  output [1:0] ALUfunc
);

  wire not_1_out, not_2_out;

  not not_1 (not_1_out, Opcode[1]);
  not not_2 (not_2_out, Opcode[0]);
  and and_1 (mux1[1], Opcode[0], Opcode[1]);
  and and_2 (MR, not_1_out, Opcode[0]);
  or or_1 (mux2, Opcode[1], Opcode[0]);
  or or_2 (WE, not_1_out, Opcode[0]);
  and and_3 (MW, not_2_out, Opcode[1]);

  assign ALUfunc = Opcode[3:2];
  assign mux1[0] = MR;
endmodule
