// Logisim project mert_2453025.circ as structural Verilog: 6 circuits, main circuit main
module main (
  input  in_1,
  input  in_2,
  input  in_3
);

  wire alu_8_1_eq, clock_1_out, controlunit_1_mux2, controlunit_1_read, controlunit_1_we, controlunit_1_write;
  wire [1:0] and_1_out, controlunit_1_mux1, controlunit_1_pcmux;
  wire [1:1] controlunit_1_branch;
  wire [2:0] controlunit_1_alufunc;
  wire [7:0] alu_8_1_result, multiplexer_2_out, multiplexer_3_out, ramm_1_outp, regfile_1_data1,
       regfile_1_data2;
  wire [9:0] adder_1_out, adder_2_out, multiplexer_1_out, register_1_q, romm_1_data;
  wire [20:10] romm_1_data_2;

  Clock clock_1 (.out(clock_1_out));
  Register #(.trigger("falling"), .width(10)) register_1 (
    .D(multiplexer_1_out), .clk(clock_1_out), .Q(register_1_q), .clr(in_3));  // open: en
  Multiplexer #(.select(2), .width(10)) multiplexer_1 (
    .in0(adder_1_out), .in1(adder_2_out), .in2(romm_1_data), .out(multiplexer_1_out), .sel(and_1_out));  // open: in3
  Adder #(.width(10)) adder_1 (.a(10'h1), .b(register_1_q), .out(adder_1_out), .cin(in_2));  // open: cout
  ROMM romm_1 (.address(register_1_q), .data({romm_1_data_2, romm_1_data}));
  Multiplexer #(.select(2), .width(8)) multiplexer_2 (
    .in0(alu_8_1_result), .in1(ramm_1_outp), .in2(romm_1_data[7:0]), .out(multiplexer_2_out),
    .sel(controlunit_1_mux1));  // open: in3
  assign and_1_out = {2{controlunit_1_branch[1]}} & controlunit_1_pcmux;  // AND_Gate and_1, 2 bits wide
  Adder #(.width(10)) adder_2 (
    .a(register_1_q), .b({romm_1_data[7:0], romm_1_data[7:6]}), .out(adder_2_out), .cin(in_1));  // open: cout
  ControlUnit controlunit_1 (
    .Opcode(romm_1_data_2[20:17]), .EQ(alu_8_1_eq), .ALUfunc(controlunit_1_alufunc),
    .mux1(controlunit_1_mux1), .mux2(controlunit_1_mux2), .WE(controlunit_1_we), .Write(controlunit_1_write),
    .Read(controlunit_1_read), .PCmux(controlunit_1_pcmux), .Branch(controlunit_1_branch[1]));
  RegFile regfile_1 (
    .WE(controlunit_1_we), .writeRegister({romm_1_data_2[10], romm_1_data[9:8]}),
    .writeData(multiplexer_2_out), .read1(romm_1_data_2[16:14]), .read2(romm_1_data_2[13:11]),
    .data1(regfile_1_data1), .data2(regfile_1_data2));
  Multiplexer #(.width(8)) multiplexer_3 (
    .in0(regfile_1_data2), .in1(romm_1_data[7:0]), .out(multiplexer_3_out), .sel(controlunit_1_mux2));
  ALU_8 alu_8_1 (
    .X(regfile_1_data1), .Y(multiplexer_3_out), .ALUfunc(controlunit_1_alufunc), .RESULT(alu_8_1_result),
    .EQ(alu_8_1_eq));
  RAMM ramm_1 (
    .address(alu_8_1_result), .WE(controlunit_1_write), .OutE(controlunit_1_read), .inp(regfile_1_data2),
    .outp(ramm_1_outp));
endmodule

module ALU_8 (
  input  [7:0] X,
  input  [7:0] Y,
  input  [2:0] ALUfunc,
  output [7:0] RESULT,
  output EQ
);

  wire [0:0] comparator_1_lt;
  wire [7:0] adder_1_out, and_1_out, or_1_out, shifter_1_out, xnor_1_out;

  Comparator comparator_1 (.a(X), .b(Y), .lt(comparator_1_lt[0]));  // open: gt, eq
  Adder adder_1 (.a(X), .b(Y), .out(adder_1_out));  // open: cin, cout
  Shifter #(.shift("rl")) shifter_1 (.in(X), .\dist (Y[2:0]), .out(shifter_1_out));
  assign and_1_out = X & Y;  // AND_Gate and_1, 8 bits wide
  assign or_1_out = X | Y;  // OR_Gate or_1, 8 bits wide
  assign xnor_1_out = ~(Y ^ X);  // XNOR_Gate xnor_1, 8 bits wide
  Multiplexer #(.select(3), .width(8)) multiplexer_1 (
    .in0(adder_1_out), .in1(and_1_out), .in2(or_1_out), .in3(shifter_1_out),
    .in4({{7{1'b0}}, comparator_1_lt[0]}), .out(RESULT), .sel(ALUfunc));  // open: in5, in6, in7
  and and_2 (EQ, xnor_1_out[0], xnor_1_out[1], xnor_1_out[2], xnor_1_out[3], xnor_1_out[4], xnor_1_out[5], xnor_1_out[6], xnor_1_out[7]);
endmodule

module RAMM (
  input  [7:0] address,
  input  WE,
  input  OutE,
  input  [7:0] inp,
  output [7:0] outp
);

  wire Clk_out;

  Clock Clk (.out(Clk_out));
  RAM #(.asyncread("true"), .trigger("falling")) ram_1 (
    .addr(address), .we(WE), .oe(OutE), .clk(Clk_out), .din(inp), .dout(outp));
endmodule

module ROMM (
  input  [9:0] address,
  output [20:0] data
);

  ROM #(.addrWidth(10), .dataWidth(21), .misaligned("true")) ProgramROM (.addr(address), .data(data));

  // Notes on the sheet:
  //   contents of ProgramROM (hex, n*v repeats v):
  //   60206 60501 6030c 1ae00 1ef400 b2882 160008 6900
endmodule

module RegFile (
  input  WE,
  input  [2:0] writeRegister,
  input  [7:0] writeData,
  input  [2:0] read1,
  input  [2:0] read2,
  output [7:0] data1,
  output [7:0] data2
);

  wire clock_1_out, decoder_1_out0, decoder_1_out1, decoder_1_out2, decoder_1_out3, decoder_1_out4,
       decoder_1_out5, decoder_1_out6, decoder_1_out7;
  wire [7:0] register_1_q, register_2_q, register_3_q, register_4_q, register_5_q, register_6_q,
       register_7_q, register_8_q;

  Decoder #(.select(3)) decoder_1 (
    .out0(decoder_1_out0), .out1(decoder_1_out1), .out2(decoder_1_out2), .out3(decoder_1_out3),
    .out4(decoder_1_out4), .out5(decoder_1_out5), .out6(decoder_1_out6), .out7(decoder_1_out7),
    .sel(writeRegister), .en(WE));
  Clock clock_1 (.out(clock_1_out));
  Multiplexer #(.select(3), .width(8)) multiplexer_1 (
    .in0(register_1_q), .in1(register_2_q), .in2(register_3_q), .in3(register_4_q), .in4(register_5_q),
    .in5(register_6_q), .in6(register_7_q), .in7(register_8_q), .out(data1), .sel(read1));
  Multiplexer #(.select(3), .width(8)) multiplexer_2 (
    .in0(register_1_q), .in1(register_2_q), .in2(register_3_q), .in3(register_4_q), .in4(register_5_q),
    .in5(register_6_q), .in6(register_7_q), .in7(register_8_q), .out(data2), .sel(read2));
  Register #(.trigger("falling")) register_1 (
    .D(writeData), .en(decoder_1_out0), .clk(clock_1_out), .Q(register_1_q));  // open: clr
  Register #(.trigger("falling")) register_2 (
    .D(writeData), .en(decoder_1_out1), .clk(clock_1_out), .Q(register_2_q));  // open: clr
  Register #(.trigger("falling")) register_3 (
    .D(writeData), .en(decoder_1_out2), .clk(clock_1_out), .Q(register_3_q));  // open: clr
  Register #(.trigger("falling")) register_4 (
    .D(writeData), .en(decoder_1_out3), .clk(clock_1_out), .Q(register_4_q));  // open: clr
  Register #(.trigger("falling")) register_5 (
    .D(writeData), .en(decoder_1_out4), .clk(clock_1_out), .Q(register_5_q));  // open: clr
  Register #(.trigger("falling")) register_6 (
    .D(writeData), .en(decoder_1_out5), .clk(clock_1_out), .Q(register_6_q));  // open: clr
  Register #(.trigger("falling")) register_7 (
    .D(writeData), .en(decoder_1_out6), .clk(clock_1_out), .Q(register_7_q));  // open: clr
  Register #(.trigger("falling")) register_8 (
    .D(writeData), .en(decoder_1_out7), .clk(clock_1_out), .Q(register_8_q));  // open: clr
endmodule

module ControlUnit (
  input  [3:0] Opcode,
  input  EQ,
  output [2:0] ALUfunc,
  output [1:0] mux1,
  output mux2,
  output WE,
  output Write,
  output Read,
  output [1:0] PCmux,
  output Branch
);

  wire and_6_out, and_7_out, and_8_out, and_13_out, and_14_out, and_15_out, not_1_out, not_2_out, not_3_out,
       not_4_out, not_5_out, not_6_out, not_7_out, not_8_out, not_9_out, or_1_out;

  not not_1 (not_1_out, EQ);
  not not_2 (not_2_out, Opcode[0]);
  not not_3 (not_3_out, Opcode[1]);
  not not_4 (not_4_out, Opcode[2]);
  not not_5 (not_5_out, Opcode[2]);
  not not_6 (not_6_out, Opcode[0]);
  not not_7 (not_7_out, Opcode[3]);
  not not_8 (not_8_out, Opcode[1]);
  and and_1 (ALUfunc[2], Opcode[0], Opcode[1], Opcode[2], Opcode[3]);
  and and_2 (ALUfunc[1], not_2_out, not_3_out, Opcode[3]);
  and and_3 (ALUfunc[0], not_3_out, not_2_out, Opcode[2]);
  and and_4 (mux1[1], not_4_out, Opcode[1], Opcode[0]);
  and and_5 (mux1[0], not_3_out, Opcode[0]);
  or or_1 (or_1_out, Opcode[1], Opcode[0]);
  not not_9 (not_9_out, Opcode[1]);
  and and_6 (and_6_out, not_3_out, not_6_out);
  and and_7 (and_7_out, not_7_out, not_4_out, Opcode[0]);
  and and_8 (and_8_out, Opcode[3], Opcode[2]);
  and and_9 (Write, not_6_out, Opcode[1]);
  and and_10 (Read, not_4_out, not_8_out, Opcode[0]);
  and and_11 (PCmux[0], not_7_out, Opcode[2], Opcode[0]);
  and and_12 (PCmux[1], Opcode[3], not_4_out, Opcode[1]);
  and and_13 (and_13_out, not_7_out, Opcode[2], not_1_out, Opcode[1], Opcode[0]);
  and and_14 (and_14_out, not_7_out, Opcode[2], not_9_out, Opcode[0], EQ);
  and and_15 (and_15_out, Opcode[3], not_5_out, Opcode[1], Opcode[0]);
  and and_16 (mux2, not_4_out, or_1_out);
  or or_2 (WE, and_6_out, and_7_out, and_8_out);
  or or_3 (Branch, and_13_out, and_14_out, and_15_out);
endmodule
